# Fritzing sketch Extension_C1.3. (saved by Fritzing 0.9.3b)
circuit board: 7.4656cm x 11.0585cm
breadboards: 1

parts:
  U3 = RJ45 Jack [package=rj45-8]
  Bauteil1 = Arduino Pro Mini v13
  5V_B_A_GND = female pin header, 4 pins [form="♀ (female)"]
  DI_DE_RE_RO1 = female pin header, 4 pins [form="♀ (female)"]
  C6 = Ceramic Capacitor [capacitance=100nF package="100 mil [THT, multilayer]"]
  C7 = Tantalum Capacitor [capacitance=330nF voltage=35V package="100 mil [THT, tantalum]"]
  U4 = RJ45 Jack [package=rj45-8]
  SW4 = DIP Switch 4 Position [package=dipswitch-04]
  3_3k6 = Resistor [tolerance=±5% resistance=68k package=THT]
  3_3k7 = Resistor [tolerance=±5% resistance=33k package=THT]
  3_3k8 = Resistor [tolerance=±5% resistance=15k package=THT]
  3_3k9 = Resistor [tolerance=±5% resistance=6.8k package=THT]
  3_3k10 = Resistor [tolerance=±5% resistance=3.3k package=THT]
  Vreg_5V = Voltage Regulator - 5V [package="TO220 [THT]"]
  Vreg_12V = Voltage Regulator - 5V [package="TO220 [THT]"]
  C8 = Ceramic Capacitor [capacitance=100nF package="100 mil [THT, multilayer]"]
  J10 = female pin header, 2 pins [form="♀ (female)"]
  J11 = female pin header, 2 pins [form="♀ (female)"]
  ULN2803A2 = ULN2803A [package=THT]
  ULN2803A3 = ULN2803A [package=THT]
  ULN2803A4 = ULN2803A [package=THT]
  ULN2803A5 = ULN2803A [package=THT]
  ULN2803A6 = ULN2803A [package=THT]

nets:
  N1: U3.1, 5V_B_A_GND.pin2, U4.1
  N2: U3.2, 5V_B_A_GND.pin3, U4.2
  GND: U3.3, U3.5, U3.7, Bauteil1.GND, 5V_B_A_GND.pin4, C6.1, C7.-, U4.3, U4.5, U4.7, 3_3k10.Pin_1, Vreg_5V.GND, Vreg_12V.GND, C8.1, ULN2803A2.0V
  N3: U3.4, U3.6, U3.8, C7.+, U4.4, U4.6, U4.8, Vreg_5V.input_voltage, Vreg_12V.input_voltage
  N4: Bauteil1.D0/TX, DI_DE_RE_RO1.pin1
  N5: Bauteil1.D1/RX, DI_DE_RE_RO1.pin4
  N6: Bauteil1.VCC, 5V_B_A_GND.pin1, SW4.5, SW4.6, SW4.7, SW4.8, J10.pin1, ULN2803A2.COM_-_Common
  N7: Bauteil1.RAW, J11.pin1
  N8: Bauteil1.A3, 3_3k6.Pin_0, 3_3k7.Pin_0, 3_3k8.Pin_0, 3_3k9.Pin_0, 3_3k10.Pin_0
  N9: Bauteil1.A0, ULN2803A2.In_1
  N10: Bauteil1.D13/SCK, DI_DE_RE_RO1.pin2, DI_DE_RE_RO1.pin3
  N11: Bauteil1.D12/MISO, ULN2803A2.In_2
  N12: Bauteil1.D11_PWM/MOSI, ULN2803A2.In_3
  N13: Bauteil1.D10_PWM/SS, ULN2803A2.In_4
  N14: Bauteil1.D9_PWM, ULN2803A3.In_1, ULN2803A4.In_1, ULN2803A5.In_1, ULN2803A6.In_1
  N15: Bauteil1.D8, ULN2803A3.In_2, ULN2803A4.In_2, ULN2803A5.In_2, ULN2803A6.In_2
  N16: Bauteil1.D7, ULN2803A3.In_3, ULN2803A4.In_3, ULN2803A5.In_3, ULN2803A6.In_3
  N17: Bauteil1.D6_PWM, ULN2803A3.In_4, ULN2803A4.In_4, ULN2803A5.In_4, ULN2803A6.In_4
  N18: Bauteil1.D5_PWM, ULN2803A3.In_5, ULN2803A4.In_5, ULN2803A5.In_5, ULN2803A6.In_5
  N19: Bauteil1.D4, ULN2803A3.In_6, ULN2803A4.In_6, ULN2803A5.In_6, ULN2803A6.In_6
  N20: Bauteil1.D3_PWM, ULN2803A3.In_7, ULN2803A4.In_7, ULN2803A5.In_7, ULN2803A6.In_7
  N21: Bauteil1.D2, ULN2803A3.In_8, ULN2803A4.In_8, ULN2803A5.In_8, ULN2803A6.In_8
  N22: C6.0, Vreg_12V.output_voltage, J11.pin2, ULN2803A3.COM_-_Common, ULN2803A4.COM_-_Common, ULN2803A5.COM_-_Common, ULN2803A6.COM_-_Common
  N23: SW4.1, 3_3k9.Pin_1
  N24: SW4.2, 3_3k8.Pin_1
  N25: SW4.3, 3_3k7.Pin_1
  N26: SW4.4, 3_3k6.Pin_1
  N27: Vreg_5V.output_voltage, C8.0, J10.pin2
  N28: ULN2803A2.Out_4, ULN2803A3.0V
  N29: ULN2803A2.Out_3, ULN2803A4.0V
  N30: ULN2803A2.Out_2, ULN2803A5.0V
  N31: ULN2803A2.Out_1, ULN2803A6.0V

notes:
  IsWISaS_Extension_C1.2
  https://github.com/stseeger/IsWISaS
  +
  -
  5V->VCC
  12V->RAW
